# Fritzing sketch Board (saved by Fritzing 0.9.3b)
circuit board: 4.77511cm x 4.01713cm
breadboards: 2

parts:
  NodeMCU_v1 = NodeMCU v3 LoLin [part_number=ESP8266]
  Q1 = NPN-Transistor [part_number=ZT2115 package="TO92 [THT]"]
  LED3 = LED - 5mm [color="Infrared (940nm)" part_number=ZD1945 package="5 mm [THT]"]
  R1 = Resistor [tolerance=±5% resistance=200 package=THT]
  Part1 = KY-015 Temperature & Humidity Sensor Module [package="Breakout board"]

nets:
  N1: NodeMCU_v1.D4, Part1.S
  3V3: NodeMCU_v1.3V3, Part1.Vin
  N2: NodeMCU_v1.GND#6, NodeMCU_v1.GND#16, NodeMCU_v1.GND#33, Part1.-
  N3: NodeMCU_v1.D5, R1.Pin_1
  N4: NodeMCU_v1.VU, LED3.anode
  N5: NodeMCU_v1.GND#41, Q1.E
  N6: Q1.B, LED3.cathode
  N7: Q1.C, R1.Pin_0

custom parts:
  NodeMCU v3 LoLin: NodeMCU v3 LoLin NodeMCU (http://www.nodemcu.com/) is an open source IoT platform. It includes firmware (https://nodemcu-build.com/) which runs on the ESP8266 Wi-Fi SoC from Espressif Systems, and hardware which is based on the ESP-12E module. The term "NodeMCU" by default refers to the firmware rather than the dev kits. The firmware uses the Lua scripting language. It is based on the eLua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
  KY-015 Temperature & Humidity Sensor Module: KY-015 temperature and humidity sensor module, provides a low-latency serial interface to measure humidity and temperature.
